// Logisim project pipelined_CPU.circ as structural Verilog: 13 circuits, main circuit main
module main (
  input  CLR,
  output [31:0] out_2,
  output [31:0] out_3,
  output out_4,
  output [4:0] out_5,
  output [31:0] out_6,
  output out_7,
  output [31:0] out_8,
  output [31:0] out_9
);

  wire Branch_jr, controller_1_alusel, controller_1_branch_beq, controller_1_branch_bne,
       controller_1_branch_j_jal, controller_1_memread, controller_1_memwrite, controller_1_regwrite,
       ex_mem_1_memread_m, ex_mem_1_regwrite_m, id_ex_1_alusel_e, id_ex_1_memread_e, id_ex_1_memwrite_e,
       id_ex_1_regwrite_e, Zero;
  wire [1:0] controller_1_dmmode, controller_1_extop, controller_1_wasel, controller_1_wdsel,
       ex_mem_1_dmmode_m, ex_mem_1_wdsel_m, id_ex_1_dmmode_e, id_ex_1_wdsel_e, mem_wb_1_wdsel_w;
  wire [2:0] ALUOp;
  wire [3:0] alu_controller_1_aluctrl, id_ex_1_aluctrl_e;
  wire [4:0] ex_mem_1_regaddr_m, id_ex_1_regaddr_e, id_ex_1_shamt_e, multiplexer_1_out, splitter_1_rd,
       splitter_1_rs, splitter_1_rt, splitter_1_shamt;
  wire [5:0] splitter_1_func, splitter_1_op;
  wire [15:0] splitter_1_imm16_out;
  wire [25:0] splitter_1_imm26_out;
  wire [31:0] alu_1_result, dm_1_out_7, ex_mem_1_pc_8_m, ext_1_imm32, grf_1_rd2, id_ex_1_imm32_e,
       id_ex_1_imm32_e_2, id_ex_1_pc_e, id_ex_1_rd1_e, id_ex_1_rd2_e, if_id_1_instr_d, if_id_1_pc_4_d,
       if_id_1_pc_8_d, if_id_1_pc_d, ifu_1_instr, ifu_1_pc, ifu_1_pc_4, ifu_1_pc_8, mem_wb_1_pc_8_w,
       mem_wb_1_rd_w, mem_wb_1_result_w, multiplexer_2_out, rs;

  IFU ifu_1 (
    .imm16_in(splitter_1_imm16_out), .ReadReg(rs), .imm26_in(splitter_1_imm26_out),
    .Branch_beq(controller_1_branch_beq), .Branch_bne(controller_1_branch_bne),
    .Branch_j_jal(controller_1_branch_j_jal), .Branch_jr(Branch_jr), .PC_4(ifu_1_pc_4), .Instr(ifu_1_instr),
    .Zero(Zero), .CLR(CLR), .PC(ifu_1_pc), .PC_8(ifu_1_pc_8), .PC_4_Br(if_id_1_pc_4_d), .PC_J(if_id_1_pc_d));
  IF_ID if_id_1 (
    .Instr_F(ifu_1_instr), .CLR(CLR), .Instr_D(if_id_1_instr_d), .PC_4_F(ifu_1_pc_4),
    .PC_4_D(if_id_1_pc_4_d), .PC_F(ifu_1_pc), .PC_D(if_id_1_pc_d), .PC_8_F(ifu_1_pc_8),
    .PC_8_D(if_id_1_pc_8_d));
  Splitter splitter_1 (
    .Instr(if_id_1_instr_d), .op(splitter_1_op), .rs(splitter_1_rs), .rt(splitter_1_rt), .rd(splitter_1_rd),
    .shamt(splitter_1_shamt), .func(splitter_1_func), .imm16_out(splitter_1_imm16_out),
    .imm26_out(splitter_1_imm26_out));
  Controller controller_1 (
    .op(splitter_1_op), .Branch_bne(controller_1_branch_bne), .Branch_beq(controller_1_branch_beq),
    .Branch_j_jal(controller_1_branch_j_jal), .RegWrite(controller_1_regwrite),
    .MemWrite(controller_1_memwrite), .MemRead(controller_1_memread), .ALUSel(controller_1_alusel),
    .WDSel(controller_1_wdsel), .WASel(controller_1_wasel), .EXTOp(controller_1_extop), .ALUOp(ALUOp),
    .DMMode(controller_1_dmmode));
  ALU_Controller alu_controller_1 (
    .func(splitter_1_func), .ALUOp(ALUOp), .ALUCtrl(alu_controller_1_aluctrl), .Branch_jr(Branch_jr));
  Multiplexer #(.select(2), .width(5), .enable("false")) multiplexer_1 (
    .in0(splitter_1_rd), .in1(splitter_1_rt), .in2({5{1'b1}}), .out(multiplexer_1_out),
    .sel(controller_1_wasel));  // open: in3
  GRF grf_1 (
    .WD(out_6), .A3(out_5), .A1(splitter_1_rs), .A2(splitter_1_rt), .RD1(rs), .RD2(grf_1_rd2), .reset(CLR),
    .WE(out_4));
  Comparator #(.width(32)) comparator_1 (.a(rs), .b(grf_1_rd2), .eq(Zero));  // open: gt, lt
  EXT ext_1 (.imm16(splitter_1_imm16_out), .imm32(ext_1_imm32), .EXTOp(controller_1_extop));
  ID_EX id_ex_1 (
    .CLR(CLR), .MemWrite_D(controller_1_memwrite), .MemRead_D(controller_1_memread),
    .RegAddr_D(multiplexer_1_out), .shamt_D(splitter_1_shamt), .ALUSel_D(controller_1_alusel),
    .WDSel_D(controller_1_wdsel), .RegWrite_D(controller_1_regwrite), .ALUCtrl_D(alu_controller_1_aluctrl),
    .RD1_D(rs), .RD2_D(grf_1_rd2), .imm32_D(ext_1_imm32), .MemWrite_E(id_ex_1_memwrite_e),
    .MemRead_E(id_ex_1_memread_e), .RegAddr_E(id_ex_1_regaddr_e), .shamt_E(id_ex_1_shamt_e),
    .ALUSel_E(id_ex_1_alusel_e), .WDSel_E(id_ex_1_wdsel_e), .RegWrite_E(id_ex_1_regwrite_e),
    .ALUCtrl_E(id_ex_1_aluctrl_e), .RD1_E(id_ex_1_rd1_e), .RD2_E(id_ex_1_rd2_e), .imm32_E(id_ex_1_imm32_e),
    .PC_8_D(if_id_1_pc_8_d), .imm32_E_2(id_ex_1_imm32_e_2), .PC_D(if_id_1_pc_d), .PC_E(id_ex_1_pc_e),
    .DMMode_D(controller_1_dmmode), .DMMode_E(id_ex_1_dmmode_e));
  Multiplexer #(.width(32), .enable("false")) multiplexer_2 (
    .in0(id_ex_1_rd2_e), .in1(id_ex_1_imm32_e), .out(multiplexer_2_out), .sel(id_ex_1_alusel_e));
  ALU alu_1 (
    .A(id_ex_1_rd1_e), .B(multiplexer_2_out), .Result(alu_1_result), .ALUCtrl(id_ex_1_aluctrl_e),
    .shamt(id_ex_1_shamt_e));  // open: Zero
  EX_MEM ex_mem_1 (
    .CLR(CLR), .MemWrite_E(id_ex_1_memwrite_e), .MemRead_E(id_ex_1_memread_e), .RegAddr_E(id_ex_1_regaddr_e),
    .WDSel_E(id_ex_1_wdsel_e), .RegWrite_E(id_ex_1_regwrite_e), .Result_E(alu_1_result),
    .RD2_E(id_ex_1_rd2_e), .PC_8_E(id_ex_1_imm32_e_2), .MemWrite_M(out_7), .MemRead_M(ex_mem_1_memread_m),
    .RegAddr_M(ex_mem_1_regaddr_m), .WDSel_M(ex_mem_1_wdsel_m), .RegWrite_M(ex_mem_1_regwrite_m),
    .Result_M(out_8), .RD2_M(out_9), .PC_8_M(ex_mem_1_pc_8_m), .PC_E(id_ex_1_pc_e), .PC_M(out_3),
    .DMMode_E(id_ex_1_dmmode_e), .DMMode_M(ex_mem_1_dmmode_m));
  DM dm_1 (
    .in_2(out_8), .in_6(out_9), .out_7(dm_1_out_7), .in_3(out_7), .in_4(ex_mem_1_memread_m), .in_5(CLR),
    .DMMode(ex_mem_1_dmmode_m));
  MEM_WB mem_wb_1 (
    .PC_M(out_3), .RegAddr_M(ex_mem_1_regaddr_m), .WDSel_M(ex_mem_1_wdsel_m),
    .RegWrite_M(ex_mem_1_regwrite_m), .Result_M(out_8), .RD_M(dm_1_out_7), .PC_8_M(ex_mem_1_pc_8_m),
    .PC_W(out_2), .RegAddr_W(out_5), .WDSel_W(mem_wb_1_wdsel_w), .RegWrite_W(out_4),
    .Result_W(mem_wb_1_result_w), .RD_W(mem_wb_1_rd_w), .PC_8_W(mem_wb_1_pc_8_w));  // open: CLR
  Multiplexer #(.select(2), .width(32), .enable("false")) multiplexer_3 (
    .in0(mem_wb_1_result_w), .in1(mem_wb_1_rd_w), .in2(mem_wb_1_pc_8_w), .out(out_6), .sel(mem_wb_1_wdsel_w));  // open: in3

  // Other names for the same wires on the sheet: MemAddr[31:0] = out_8; MemData[31:0] = out_9; MemWrite = out_7;
  //   PC_M[31:0] = out_3; PC_W[31:0] = out_2; RegAddr[4:0] = out_5; RegData[31:0] = out_6; RegWrite = out_4
endmodule

module GRF (
  input  reset,
  input  WE,
  input  [31:0] WD,
  input  [4:0] A3,
  input  [4:0] A1,
  input  [4:0] A2,
  output [31:0] RD1,
  output [31:0] RD2
);

  wire and_1_out, and_2_out, and_3_out, and_4_out, and_5_out, and_6_out, and_7_out, and_8_out, and_9_out,
       and_10_out, and_11_out, and_12_out, and_13_out, and_14_out, and_15_out, and_16_out, and_17_out,
       and_18_out, and_19_out, and_20_out, and_21_out, and_22_out, and_23_out, and_24_out, and_25_out,
       and_26_out, and_27_out, and_28_out, and_29_out, and_30_out, and_31_out, and_32_out, bitselector_1_out,
       bitselector_2_out, bitselector_3_out, bitselector_4_out, bitselector_5_out, bitselector_6_out,
       bitselector_7_out, bitselector_8_out, bitselector_9_out, bitselector_10_out, bitselector_11_out,
       bitselector_12_out, bitselector_13_out, bitselector_14_out, bitselector_15_out, bitselector_16_out,
       bitselector_17_out, bitselector_18_out, bitselector_19_out, bitselector_20_out, bitselector_21_out,
       bitselector_22_out, bitselector_23_out, bitselector_24_out, bitselector_25_out, bitselector_26_out,
       bitselector_27_out, bitselector_28_out, bitselector_29_out, bitselector_30_out, bitselector_31_out,
       bitselector_32_out, CLK;
  wire [7:0] decoder_1_out0, decoder_1_out8, decoder_1_out16, decoder_1_out24;
  wire [31:0] O0, O1, O2, O3, O4, O5, O6, O7, O8, O9, O10, O11, O12, O13, O14, O15, O16, O17, O18, O19, O20,
       O21, O22, O23, O24, O25, O26, O27, O28, O29, O30, O31;

  Decoder #(.select(5), .enable("false")) decoder_1 (
    .out0(decoder_1_out0[0]), .out1(decoder_1_out0[1]), .out2(decoder_1_out0[2]), .out3(decoder_1_out0[3]),
    .out4(decoder_1_out0[4]), .out5(decoder_1_out0[5]), .out6(decoder_1_out0[6]), .out7(decoder_1_out0[7]),
    .out8(decoder_1_out8[0]), .out9(decoder_1_out8[1]), .out10(decoder_1_out8[2]), .out11(decoder_1_out8[3]),
    .out12(decoder_1_out8[4]), .out13(decoder_1_out8[5]), .out14(decoder_1_out8[6]),
    .out15(decoder_1_out8[7]), .out16(decoder_1_out16[0]), .out17(decoder_1_out16[1]),
    .out18(decoder_1_out16[2]), .out19(decoder_1_out16[3]), .out20(decoder_1_out16[4]),
    .out21(decoder_1_out16[5]), .out22(decoder_1_out16[6]), .out23(decoder_1_out16[7]),
    .out24(decoder_1_out24[0]), .out25(decoder_1_out24[1]), .out26(decoder_1_out24[2]),
    .out27(decoder_1_out24[3]), .out28(decoder_1_out24[4]), .out29(decoder_1_out24[5]),
    .out30(decoder_1_out24[6]), .out31(decoder_1_out24[7]), .sel(A3));
  Clock clock_1 (.out(CLK));
  BitSelector bitselector_1 (.in(decoder_1_out0), .out(bitselector_1_out), .sel(3'b000));
  BitSelector bitselector_2 (.in(decoder_1_out8), .out(bitselector_2_out), .sel(3'b000));
  BitSelector bitselector_3 (.in(decoder_1_out16), .out(bitselector_3_out), .sel(3'b000));
  BitSelector bitselector_4 (.in(decoder_1_out24), .out(bitselector_4_out), .sel(3'b000));
  Register #(.width(32)) _0 (.D({32{1'b0}}), .en(and_1_out), .Q(O0), .clk(CLK), .clr(reset));
  and and_1 (and_1_out, WE, bitselector_1_out);
  Register #(.width(32)) _8 (.D(WD), .en(and_2_out), .Q(O8), .clk(CLK), .clr(reset));
  and and_2 (and_2_out, WE, bitselector_2_out);
  Register #(.width(32)) _16 (.D(WD), .en(and_3_out), .Q(O16), .clk(CLK), .clr(reset));
  and and_3 (and_3_out, WE, bitselector_3_out);
  Register #(.width(32)) _24 (.D(WD), .en(and_4_out), .Q(O24), .clk(CLK), .clr(reset));
  and and_4 (and_4_out, WE, bitselector_4_out);
  and and_5 (and_5_out, WE, bitselector_5_out);
  BitSelector bitselector_5 (.in(decoder_1_out0), .out(bitselector_5_out), .sel(3'b001));
  and and_6 (and_6_out, WE, bitselector_6_out);
  BitSelector bitselector_6 (.in(decoder_1_out8), .out(bitselector_6_out), .sel(3'b001));
  and and_7 (and_7_out, WE, bitselector_7_out);
  BitSelector bitselector_7 (.in(decoder_1_out16), .out(bitselector_7_out), .sel(3'b001));
  and and_8 (and_8_out, WE, bitselector_8_out);
  BitSelector bitselector_8 (.in(decoder_1_out24), .out(bitselector_8_out), .sel(3'b001));
  Register #(.width(32)) _1 (.D(WD), .en(and_5_out), .Q(O1), .clk(CLK), .clr(reset));
  BitSelector bitselector_9 (.in(decoder_1_out0), .out(bitselector_9_out), .sel(3'b010));
  Register #(.width(32)) _9 (.D(WD), .en(and_6_out), .Q(O9), .clk(CLK), .clr(reset));
  BitSelector bitselector_10 (.in(decoder_1_out8), .out(bitselector_10_out), .sel(3'b010));
  Register #(.width(32)) _17 (.D(WD), .en(and_7_out), .Q(O17), .clk(CLK), .clr(reset));
  BitSelector bitselector_11 (.in(decoder_1_out16), .out(bitselector_11_out), .sel(3'b010));
  Register #(.width(32)) _25 (.D(WD), .en(and_8_out), .Q(O25), .clk(CLK), .clr(reset));
  BitSelector bitselector_12 (.in(decoder_1_out24), .out(bitselector_12_out), .sel(3'b010));
  Register #(.width(32)) _2 (.D(WD), .en(and_9_out), .Q(O2), .clk(CLK), .clr(reset));
  and and_9 (and_9_out, WE, bitselector_9_out);
  Register #(.width(32)) _10 (.D(WD), .en(and_10_out), .Q(O10), .clk(CLK), .clr(reset));
  and and_10 (and_10_out, WE, bitselector_10_out);
  Register #(.width(32)) _18 (.D(WD), .en(and_11_out), .Q(O18), .clk(CLK), .clr(reset));
  and and_11 (and_11_out, WE, bitselector_11_out);
  Register #(.width(32)) _26 (.D(WD), .en(and_12_out), .Q(O26), .clk(CLK), .clr(reset));
  and and_12 (and_12_out, WE, bitselector_12_out);
  Multiplexer #(.select(5), .width(32), .enable("false")) multiplexer_1 (
    .in0(O0), .in1(O1), .in2(O2), .in3(O3), .in4(O4), .in5(O5), .in6(O6), .in7(O7), .in8(O8), .in9(O9),
    .in10(O10), .in11(O11), .in12(O12), .in13(O13), .in14(O14), .in15(O15), .in16(O16), .in17(O17),
    .in18(O18), .in19(O19), .in20(O20), .in21(O21), .in22(O22), .in23(O23), .in24(O24), .in25(O25),
    .in26(O26), .in27(O27), .in28(O28), .in29(O29), .in30(O30), .in31(O31), .out(RD1), .sel(A1));
  and and_13 (and_13_out, WE, bitselector_13_out);
  BitSelector bitselector_13 (.in(decoder_1_out0), .out(bitselector_13_out), .sel(3'b011));
  and and_14 (and_14_out, WE, bitselector_14_out);
  BitSelector bitselector_14 (.in(decoder_1_out8), .out(bitselector_14_out), .sel(3'b011));
  and and_15 (and_15_out, WE, bitselector_15_out);
  BitSelector bitselector_15 (.in(decoder_1_out16), .out(bitselector_15_out), .sel(3'b011));
  and and_16 (and_16_out, WE, bitselector_16_out);
  BitSelector bitselector_16 (.in(decoder_1_out24), .out(bitselector_16_out), .sel(3'b011));
  Register #(.width(32)) _3 (.D(WD), .en(and_13_out), .Q(O3), .clk(CLK), .clr(reset));
  Register #(.width(32)) _11 (.D(WD), .en(and_14_out), .Q(O11), .clk(CLK), .clr(reset));
  Register #(.width(32)) _19 (.D(WD), .en(and_15_out), .Q(O19), .clk(CLK), .clr(reset));
  Register #(.width(32)) _27 (.D(WD), .en(and_16_out), .Q(O27), .clk(CLK), .clr(reset));
  and and_17 (and_17_out, WE, bitselector_17_out);
  BitSelector bitselector_17 (.in(decoder_1_out0), .out(bitselector_17_out), .sel(3'b100));
  and and_18 (and_18_out, WE, bitselector_18_out);
  BitSelector bitselector_18 (.in(decoder_1_out8), .out(bitselector_18_out), .sel(3'b100));
  and and_19 (and_19_out, WE, bitselector_19_out);
  BitSelector bitselector_19 (.in(decoder_1_out16), .out(bitselector_19_out), .sel(3'b100));
  and and_20 (and_20_out, WE, bitselector_20_out);
  BitSelector bitselector_20 (.in(decoder_1_out24), .out(bitselector_20_out), .sel(3'b100));
  Register #(.width(32)) _4 (.D(WD), .en(and_17_out), .Q(O4), .clk(CLK), .clr(reset));
  BitSelector bitselector_21 (.in(decoder_1_out0), .out(bitselector_21_out), .sel(3'b101));
  Register #(.width(32)) _12 (.D(WD), .en(and_18_out), .Q(O12), .clk(CLK), .clr(reset));
  BitSelector bitselector_22 (.in(decoder_1_out8), .out(bitselector_22_out), .sel(3'b101));
  Register #(.width(32)) _20 (.D(WD), .en(and_19_out), .Q(O20), .clk(CLK), .clr(reset));
  BitSelector bitselector_23 (.in(decoder_1_out16), .out(bitselector_23_out), .sel(3'b101));
  Register #(.width(32)) _28 (.D(WD), .en(and_20_out), .Q(O28), .clk(CLK), .clr(reset));
  BitSelector bitselector_24 (.in(decoder_1_out24), .out(bitselector_24_out), .sel(3'b101));
  Register #(.width(32)) _5 (.D(WD), .en(and_21_out), .Q(O5), .clk(CLK), .clr(reset));
  and and_21 (and_21_out, WE, bitselector_21_out);
  Register #(.width(32)) _13 (.D(WD), .en(and_22_out), .Q(O13), .clk(CLK), .clr(reset));
  and and_22 (and_22_out, WE, bitselector_22_out);
  Register #(.width(32)) _21 (.D(WD), .en(and_23_out), .Q(O21), .clk(CLK), .clr(reset));
  and and_23 (and_23_out, WE, bitselector_23_out);
  Register #(.width(32)) _29 (.D(WD), .en(and_24_out), .Q(O29), .clk(CLK), .clr(reset));
  and and_24 (and_24_out, WE, bitselector_24_out);
  and and_25 (and_25_out, WE, bitselector_25_out);
  BitSelector bitselector_25 (.in(decoder_1_out0), .out(bitselector_25_out), .sel(3'b110));
  and and_26 (and_26_out, WE, bitselector_26_out);
  BitSelector bitselector_26 (.in(decoder_1_out8), .out(bitselector_26_out), .sel(3'b110));
  and and_27 (and_27_out, WE, bitselector_27_out);
  BitSelector bitselector_27 (.in(decoder_1_out16), .out(bitselector_27_out), .sel(3'b110));
  and and_28 (and_28_out, WE, bitselector_28_out);
  BitSelector bitselector_28 (.in(decoder_1_out24), .out(bitselector_28_out), .sel(3'b110));
  Register #(.width(32)) _6 (.D(WD), .en(and_25_out), .Q(O6), .clk(CLK), .clr(reset));
  BitSelector bitselector_29 (.in(decoder_1_out0), .out(bitselector_29_out), .sel(3'b111));
  Register #(.width(32)) _14 (.D(WD), .en(and_26_out), .Q(O14), .clk(CLK), .clr(reset));
  BitSelector bitselector_30 (.in(decoder_1_out8), .out(bitselector_30_out), .sel(3'b111));
  Register #(.width(32)) _22 (.D(WD), .en(and_27_out), .Q(O22), .clk(CLK), .clr(reset));
  BitSelector bitselector_31 (.in(decoder_1_out16), .out(bitselector_31_out), .sel(3'b111));
  Register #(.width(32)) _30 (.D(WD), .en(and_28_out), .Q(O30), .clk(CLK), .clr(reset));
  BitSelector bitselector_32 (.in(decoder_1_out24), .out(bitselector_32_out), .sel(3'b111));
  Register #(.width(32)) _7 (.D(WD), .en(and_29_out), .Q(O7), .clk(CLK), .clr(reset));
  and and_29 (and_29_out, WE, bitselector_29_out);
  Register #(.width(32)) _15 (.D(WD), .en(and_30_out), .Q(O15), .clk(CLK), .clr(reset));
  and and_30 (and_30_out, WE, bitselector_30_out);
  Register #(.width(32)) _23 (.D(WD), .en(and_31_out), .Q(O23), .clk(CLK), .clr(reset));
  and and_31 (and_31_out, WE, bitselector_31_out);
  Register #(.width(32)) _31 (.D(WD), .en(and_32_out), .Q(O31), .clk(CLK), .clr(reset));
  and and_32 (and_32_out, WE, bitselector_32_out);
  Multiplexer #(.select(5), .width(32), .enable("false")) multiplexer_2 (
    .in0(O0), .in1(O1), .in2(O2), .in3(O3), .in4(O4), .in5(O5), .in6(O6), .in7(O7), .in8(O8), .in9(O9),
    .in10(O10), .in11(O11), .in12(O12), .in13(O13), .in14(O14), .in15(O15), .in16(O16), .in17(O17),
    .in18(O18), .in19(O19), .in20(O20), .in21(O21), .in22(O22), .in23(O23), .in24(O24), .in25(O25),
    .in26(O26), .in27(O27), .in28(O28), .in29(O29), .in30(O30), .in31(O31), .out(RD2), .sel(A2));
endmodule

module DM (
  input  [1:0] DMMode,
  input  [31:0] in_2,
  input  in_3,
  input  in_4,
  input  in_5,
  input  [31:0] in_6,
  output [31:0] out_7
);

  wire clock_1_out, decoder_1_out0, decoder_1_out1, decoder_1_out2, decoder_1_out3;
  wire [1:0] _01;
  wire [7:0] bitselector_4_out, multiplexer_1_out, multiplexer_2_out, multiplexer_3_out, multiplexer_4_out,
       multiplexer_9_out;
  wire [9:0] bitselector_2_out;
  wire [15:0] bitselector_3_out, multiplexer_5_out, multiplexer_6_out, multiplexer_8_out;
  wire [31:0] bit_extender_1_out, bit_extender_2_out, multiplexer_7_out, ram_1_data, shifter_1_out;

  BitSelector #(.width(32), .group(2)) bitselector_1 (.in(in_2), .out(_01), .sel(4'b0000));
  Shifter #(.width(32), .shift("lr")) shifter_1 (.in(in_2), .\dist (5'b00010), .out(shifter_1_out));
  BitSelector #(.width(32), .group(10)) bitselector_2 (.in(shifter_1_out), .out(bitselector_2_out), .sel(2'b00));
  BitSelector #(.width(32), .group(16)) bitselector_3 (.in(in_6), .out(bitselector_3_out), .sel(1'b0));
  BitSelector #(.width(32), .group(8)) bitselector_4 (.in(in_6), .out(bitselector_4_out), .sel(2'b00));
  Multiplexer #(.width(8), .enable("false")) multiplexer_1 (
    .in0(ram_1_data[7:0]), .in1(bitselector_4_out), .out(multiplexer_1_out), .sel(decoder_1_out0));
  Multiplexer #(.width(8), .enable("false")) multiplexer_2 (
    .in0(ram_1_data[15:8]), .in1(bitselector_4_out), .out(multiplexer_2_out), .sel(decoder_1_out1));
  Multiplexer #(.width(8), .enable("false")) multiplexer_3 (
    .in0(ram_1_data[23:16]), .in1(bitselector_4_out), .out(multiplexer_3_out), .sel(decoder_1_out2));
  Multiplexer #(.width(8), .enable("false")) multiplexer_4 (
    .in0(ram_1_data[31:24]), .in1(bitselector_4_out), .out(multiplexer_4_out), .sel(decoder_1_out3));
  Multiplexer #(.width(16), .enable("false")) multiplexer_5 (
    .in0(ram_1_data[15:0]), .in1(bitselector_3_out), .out(multiplexer_5_out), .sel(decoder_1_out0));
  Multiplexer #(.width(16), .enable("false")) multiplexer_6 (
    .in0(ram_1_data[31:16]), .in1(bitselector_3_out), .out(multiplexer_6_out), .sel(decoder_1_out2));
  Decoder #(.select(2), .enable("false")) decoder_1 (
    .out0(decoder_1_out0), .out1(decoder_1_out1), .out2(decoder_1_out2), .out3(decoder_1_out3), .sel(_01));
  Multiplexer #(.select(2), .width(32), .enable("false")) multiplexer_7 (
    .in0(in_6), .in1({multiplexer_6_out, multiplexer_5_out}),
    .in2({multiplexer_4_out, multiplexer_3_out, multiplexer_2_out, multiplexer_1_out}),
    .out(multiplexer_7_out), .sel(DMMode));  // open: in3
  Clock clock_1 (.out(clock_1_out));
  RAM #(.addrWidth(10), .dataWidth(32), .bus("separate")) ram_1 (
    .addr(bitselector_2_out), .din(multiplexer_7_out), .data(ram_1_data), .str(in_3), .clk(clock_1_out),
    .ld(in_4), .clr(in_5));  // open: sel
  Multiplexer #(.select(2), .width(16), .enable("false")) multiplexer_8 (
    .in0(ram_1_data[15:0]), .in2(ram_1_data[31:16]), .out(multiplexer_8_out), .sel(_01));  // open: in1, in3
  Multiplexer #(.select(2), .width(8), .enable("false")) multiplexer_9 (
    .in0(ram_1_data[7:0]), .in1(ram_1_data[15:8]), .in2(ram_1_data[23:16]), .in3(ram_1_data[31:24]),
    .out(multiplexer_9_out), .sel(_01));
  assign bit_extender_1_out = {{16{multiplexer_8_out[15]}}, multiplexer_8_out};  // Bit_Extender bit_extender_1
  assign bit_extender_2_out = {{24{multiplexer_9_out[7]}}, multiplexer_9_out};  // Bit_Extender bit_extender_2
  Multiplexer #(.select(2), .width(32), .enable("false")) multiplexer_10 (
    .in0(ram_1_data), .in1(bit_extender_1_out), .in2(bit_extender_2_out), .out(out_7), .sel(DMMode));  // open: in3
endmodule

module ALU (
  input  [3:0] ALUCtrl,
  input  [31:0] A,
  input  [4:0] shamt,
  input  [31:0] B,
  output [31:0] Result,
  output Zero
);

  wire comparator_1_lt;
  wire [31:0] adder_1_out, and_1_out, bit_extender_1_out, multiplexer_1_out, multiplexer_2_out,
       multiplexer_3_out, multiplexer_4_out, not_1_out, or_1_out, shifter_1_out;

  Multiplexer #(.width(32), .enable("false")) multiplexer_1 (
    .in0(B), .in1(not_1_out), .out(multiplexer_1_out), .sel(ALUCtrl[0]));
  assign not_1_out = ~B;  // NOT_Gate not_1, 32 bits wide
  assign or_1_out = A | B;  // OR_Gate or_1, 32 bits wide
  assign and_1_out = A & B;  // AND_Gate and_1, 32 bits wide
  Adder #(.width(32)) adder_1 (.a(A), .b(multiplexer_1_out), .out(adder_1_out), .cin(ALUCtrl[0]));  // open: cout
  Multiplexer #(.width(32), .enable("false")) multiplexer_2 (
    .in0(or_1_out), .in1(and_1_out), .out(multiplexer_2_out), .sel(ALUCtrl[0]));
  Shifter #(.width(32)) shifter_1 (.in(B), .\dist (shamt), .out(shifter_1_out));
  Multiplexer #(.width(32), .enable("false")) multiplexer_3 (
    .in0(adder_1_out), .in1(multiplexer_2_out), .out(multiplexer_3_out), .sel(ALUCtrl[1]));
  Comparator #(.width(32)) comparator_1 (.a(A), .b(B), .eq(Zero), .lt(comparator_1_lt));  // open: gt
  Multiplexer #(.width(32), .enable("false")) multiplexer_4 (
    .in0(multiplexer_3_out), .in1(shifter_1_out), .out(multiplexer_4_out), .sel(ALUCtrl[2]));
  assign bit_extender_1_out = {{31{1'b0}}, comparator_1_lt};  // Bit_Extender bit_extender_1
  Multiplexer #(.width(32), .enable("false")) multiplexer_5 (
    .in0(multiplexer_4_out), .in1(bit_extender_1_out), .out(Result), .sel(ALUCtrl[3]));

  // Other names for the same wires on the sheet: A0 = ALUCtrl[0]
endmodule

module IFU (
  input  Branch_beq,
  input  Branch_bne,
  input  Branch_j_jal,
  input  Branch_jr,
  input  Zero,
  input  CLR,
  input  [15:0] imm16_in,
  input  [31:0] ReadReg,
  input  [25:0] imm26_in,
  input  [31:0] PC_4_Br,
  input  [31:0] PC_J,
  output [31:0] PC_4,
  output [31:0] Instr,
  output [31:0] PC,
  output [31:0] PC_8
);

  wire and_1_out, and_2_out, clock_1_out, comparator_1_eq, or_1_out;
  wire [9:0] bitselector_2_out;
  wire [31:0] adder_3_out, imm16_Extended, multiplexer_1_out, multiplexer_2_out, multiplexer_3_out, PC_q,
       shifter_1_out, subtractor_1_out;
  wire [31:28] imm26_Extended;

  or or_1 (or_1_out, and_1_out, and_2_out);
  and and_1 (and_1_out, Branch_beq, Zero);
  Multiplexer #(.width(32), .enable("false")) multiplexer_1 (
    .in0(PC_4), .in1(adder_3_out), .out(multiplexer_1_out), .sel(or_1_out));
  and and_2 (and_2_out, ~Zero, Branch_bne);  // AND_Gate
  BitSelector #(.width(32), .group(4)) bitselector_1 (.in(PC_J), .out(imm26_Extended), .sel(3'b111));
  Multiplexer #(.width(32), .enable("false")) multiplexer_2 (
    .in0(multiplexer_1_out), .in1({imm26_Extended, imm26_in, 2'b00}), .out(multiplexer_2_out),
    .sel(Branch_j_jal));
  assign imm16_Extended = {{14{imm16_in[15]}}, {imm16_in, 2'b00}};  // Bit_Extender bit_extender_1
  Multiplexer #(.width(32), .enable("false")) multiplexer_3 (
    .in0(multiplexer_2_out), .in1(ReadReg), .out(multiplexer_3_out), .sel(Branch_jr));
  Register #(.width(32)) u_PC (.D(multiplexer_3_out), .Q(PC_q), .clk(clock_1_out), .clr(CLR));  // open: en
  Clock clock_1 (.out(clock_1_out));
  Comparator #(.width(32)) comparator_1 (.a(PC_q), .b({32{1'b0}}), .eq(comparator_1_eq));  // open: gt, lt
  Multiplexer #(.width(32), .enable("false")) multiplexer_4 (
    .in0(PC_q), .in1(32'h3000), .out(PC), .sel(comparator_1_eq));
  Subtractor #(.width(32)) subtractor_1 (.a(PC), .b(32'h3000), .out(subtractor_1_out));  // open: bin, bout
  Adder #(.width(32)) adder_1 (.a(PC), .b(32'h4), .out(PC_4));  // open: cin, cout
  BitSelector #(.width(32), .group(10)) bitselector_2 (.in(shifter_1_out), .out(bitselector_2_out), .sel(2'b00));
  Shifter #(.width(32), .shift("lr")) shifter_1 (.in(subtractor_1_out), .\dist (5'b00010), .out(shifter_1_out));
  Adder #(.width(32)) adder_2 (.a(PC_4), .b(32'h4), .out(PC_8));  // open: cin, cout
  ROM #(.addrWidth(10), .dataWidth(32)) rom_1 (.addr(bitselector_2_out), .data(Instr));  // open: sel
  Adder #(.width(32)) adder_3 (.a(PC_4_Br), .b(imm16_Extended), .out(adder_3_out));  // open: cin, cout

  // Other names for the same wires on the sheet: imm26_Extended[27:2] = imm26_in; PC_31_28[3:0] = imm26_Extended

  // Notes on the sheet:
  //   contents of rom_1 (hex, n*v repeats v):
  //   0 3c011234 4*0 34215678 4*0 ac010000 4*0 ac010004 4*0 ac010008 4*0 ac01000c 4*0 84020000 4*0
  //   84030002 4*0 80040000 4*0 80050001 4*0 80060002 4*0 80070003 4*0 3c01ffff 4*0 3421ffff 4*0 a0010001
  //   4*0 a0010007 4*0 a4010008 4*0 a401000e
endmodule

module EXT (
  input  [1:0] EXTOp,
  input  [15:0] imm16,
  output [31:0] imm32
);

  wire [31:0] bit_extender_1_out, bit_extender_2_out;

  assign bit_extender_1_out = {{16{imm16[15]}}, imm16};  // Bit_Extender bit_extender_1
  assign bit_extender_2_out = {{16{1'b0}}, imm16};  // Bit_Extender bit_extender_2
  Multiplexer #(.select(2), .width(32), .enable("false")) multiplexer_1 (
    .in0({imm16, {16{1'b0}}}), .in1(bit_extender_1_out), .in2(bit_extender_2_out), .out(imm32), .sel(EXTOp));  // open: in3
endmodule

module Controller (
  input  [5:0] op,
  output Branch_bne,
  output Branch_beq,
  output Branch_j_jal,
  output RegWrite,
  output MemWrite,
  output MemRead,
  output ALUSel,
  output [1:0] WDSel,
  output [1:0] WASel,
  output [1:0] EXTOp,
  output [2:0] ALUOp,
  output [1:0] DMMode
);

  wire andi_out, j_out, lb_out, lh_out, lui_out, lw_out, not_1_out, not_2_out, not_3_out, not_4_out,
       not_5_out, not_6_out, ori_out, sb_out, sh_out, sw_out;

  not not_1 (not_1_out, op[4]);
  not not_2 (not_2_out, op[5]);
  not not_3 (not_3_out, op[0]);
  not not_4 (not_4_out, op[1]);
  not not_5 (not_5_out, op[2]);
  not not_6 (not_6_out, op[3]);
  and R (ALUOp[2], not_2_out, not_1_out, not_6_out, not_5_out, not_4_out, not_3_out);
  and andi (andi_out, not_2_out, not_1_out, op[3], op[2], not_4_out, not_3_out);
  and ori (ori_out, not_2_out, not_1_out, op[3], op[2], not_4_out, op[0]);
  and lw (lw_out, op[5], not_1_out, not_6_out, not_5_out, op[1], op[0]);
  and sw (sw_out, op[5], not_1_out, op[3], not_5_out, op[1], op[0]);
  and beq (Branch_beq, not_2_out, not_1_out, not_6_out, op[2], not_4_out, not_3_out);
  and bne (Branch_bne, not_2_out, not_1_out, not_6_out, op[2], not_4_out, op[0]);
  and lui (lui_out, not_2_out, not_1_out, op[3], op[2], op[1], op[0]);
  and jal (WASel[1], not_2_out, not_1_out, not_6_out, not_5_out, op[1], op[0]);
  and j (j_out, not_2_out, not_1_out, not_6_out, not_5_out, op[1], not_3_out);
  and sb (sb_out, op[5], not_1_out, op[3], not_5_out, not_4_out, not_3_out);
  and sh (sh_out, op[5], not_1_out, op[3], not_5_out, not_4_out, op[0]);
  and lb (lb_out, op[5], not_1_out, not_6_out, not_5_out, not_4_out, not_3_out);
  and lh (lh_out, op[5], not_1_out, not_6_out, not_5_out, not_4_out, op[0]);
  or or_1 (Branch_j_jal, WASel[1], j_out);
  or or_2 (RegWrite, lb_out, ALUOp[2], andi_out, ori_out, lw_out, lui_out, WASel[1], lh_out);
  or or_3 (MemWrite, sb_out, sw_out, sh_out);
  or or_4 (MemRead, sb_out, sh_out, lw_out, lb_out, lh_out);
  or or_5 (ALUSel, sb_out, sh_out, andi_out, ori_out, lw_out, sw_out, lui_out, lb_out, lh_out);
  or or_6 (WDSel[0], lb_out, lw_out, lh_out);
  or or_7 (WASel[0], lb_out, andi_out, ori_out, lw_out, lui_out, lh_out);
  or or_8 (EXTOp[1], andi_out, ori_out);
  or or_9 (EXTOp[0], sb_out, lw_out, sh_out, lb_out, sw_out, lh_out);
  or or_10 (ALUOp[1], andi_out, ori_out);
  or or_11 (ALUOp[0], andi_out, Branch_beq, Branch_bne);
  or or_12 (DMMode[1], sb_out, lb_out);
  or or_13 (DMMode[0], sh_out, lh_out);

  assign WDSel[1] = WASel[1];
endmodule

module ALU_Controller (
  input  [5:0] func,
  input  [2:0] ALUOp,
  output [3:0] ALUCtrl,
  output Branch_jr
);

  wire add_out, addu_2_out, addu_out, and_2_out, and_3_out, and_out, jr_out, not_1_out, not_2_out, not_3_out,
       not_4_out, not_5_out, not_6_out, not_7_out, not_8_out, not_9_out, or_2_out, or_3_out, or_out, R_out,
       sll_out, slt_out, sub_out, subu_2_out, subu_out;

  not not_1 (not_1_out, func[3]);
  not not_2 (not_2_out, func[4]);
  not not_3 (not_3_out, func[5]);
  not not_4 (not_4_out, func[0]);
  not not_5 (not_5_out, func[1]);
  not not_6 (not_6_out, func[2]);
  and addu (addu_out, func[5], not_2_out, not_1_out, not_6_out, not_5_out, func[0]);
  and subu (subu_out, func[5], not_2_out, not_1_out, not_6_out, func[1], func[0]);
  and \and  (and_out, func[5], not_2_out, not_1_out, func[2], not_5_out, not_4_out);
  and \or  (or_out, func[5], not_2_out, not_1_out, func[2], not_5_out, func[0]);
  and slt (slt_out, func[5], not_2_out, func[3], not_6_out, func[1], not_4_out);
  and sll (sll_out, not_3_out, not_2_out, not_1_out, not_6_out, not_5_out, not_4_out);
  and jr (jr_out, not_3_out, not_2_out, func[3], not_6_out, not_5_out, not_4_out);
  not not_7 (not_7_out, ALUOp[0]);
  not not_8 (not_8_out, ALUOp[1]);
  not not_9 (not_9_out, ALUOp[2]);
  and add (add_out, not_9_out, not_8_out, not_7_out);
  and sub (sub_out, not_9_out, not_8_out, ALUOp[0]);
  and or_2 (or_2_out, not_9_out, ALUOp[1], not_7_out);
  and and_2 (and_2_out, not_9_out, ALUOp[1], ALUOp[0]);
  and R (R_out, ALUOp[2], not_8_out, not_7_out);
  and addu_2 (addu_2_out, R_out, addu_out);
  and subu_2 (subu_2_out, R_out, subu_out);
  and and_3 (and_3_out, R_out, and_out);
  and or_3 (or_3_out, R_out, or_out);
  and slt_2 (ALUCtrl[3], R_out, slt_out);
  and sll_2 (ALUCtrl[2], R_out, sll_out);
  and jr_2 (Branch_jr, R_out, jr_out);
  or or_4 (ALUCtrl[1], or_2_out, and_2_out, and_3_out, or_3_out);
  or or_5 (ALUCtrl[0], sub_out, and_2_out, subu_2_out, and_3_out);
endmodule

module Splitter (
  input  [31:0] Instr,
  output [5:0] op,
  output [4:0] rs,
  output [4:0] rt,
  output [4:0] rd,
  output [4:0] shamt,
  output [5:0] func,
  output [15:0] imm16_out,
  output [25:0] imm26_out
);


  assign func = Instr[5:0];
  assign imm16_out = Instr[15:0];
  assign imm26_out = Instr[25:0];
  assign op = Instr[31:26];
  assign rd = Instr[15:11];
  assign rs = Instr[25:21];
  assign rt = Instr[20:16];
  assign shamt = Instr[10:6];
endmodule

module IF_ID (
  input  [31:0] Instr_F,
  input  [31:0] PC_F,
  input  [31:0] PC_4_F,
  input  [31:0] PC_8_F,
  input  CLR,
  output [31:0] Instr_D,
  output [31:0] PC_D,
  output [31:0] PC_4_D,
  output [31:0] PC_8_D
);

  wire clk;

  Clock clock_1 (.out(clk));
  Register #(.width(32)) register_1 (.D(Instr_F), .Q(Instr_D), .clk(clk), .clr(CLR));  // open: en
  Register #(.width(32)) register_2 (.D(PC_F), .Q(PC_D), .clk(clk), .clr(CLR));  // open: en
  Register #(.width(32)) register_3 (.D(PC_4_F), .Q(PC_4_D), .clk(clk), .clr(CLR));  // open: en
  Register #(.width(32)) register_4 (.D(PC_8_F), .Q(PC_8_D), .clk(clk), .clr(CLR));  // open: en
endmodule

module ID_EX (
  input  CLR,
  input  MemWrite_D,
  input  [31:0] PC_D,
  input  MemRead_D,
  input  [4:0] RegAddr_D,
  input  [4:0] shamt_D,
  input  ALUSel_D,
  input  [1:0] WDSel_D,
  input  RegWrite_D,
  input  [3:0] ALUCtrl_D,
  input  [31:0] RD1_D,
  input  [31:0] RD2_D,
  input  [31:0] imm32_D,
  input  [31:0] PC_8_D,
  input  [1:0] DMMode_D,
  output MemWrite_E,
  output [31:0] PC_E,
  output MemRead_E,
  output [4:0] RegAddr_E,
  output [4:0] shamt_E,
  output ALUSel_E,
  output [1:0] WDSel_E,
  output RegWrite_E,
  output [3:0] ALUCtrl_E,
  output [31:0] RD1_E,
  output [31:0] RD2_E,
  output [31:0] imm32_E,
  output [31:0] imm32_E_2,
  output [1:0] DMMode_E
);

  wire clk;

  Clock clock_1 (.out(clk));
  Register #(.width(1)) register_1 (.D(MemWrite_D), .Q(MemWrite_E), .clk(clk), .clr(CLR));  // open: en
  Register #(.width(1)) register_2 (.D(MemRead_D), .Q(MemRead_E), .clk(clk), .clr(CLR));  // open: en
  Register #(.width(5)) register_3 (.D(RegAddr_D), .Q(RegAddr_E), .clk(clk), .clr(CLR));  // open: en
  Register #(.width(5)) register_4 (.D(shamt_D), .Q(shamt_E), .clk(clk), .clr(CLR));  // open: en
  Register #(.width(1)) register_5 (.D(ALUSel_D), .Q(ALUSel_E), .clk(clk), .clr(CLR));  // open: en
  Register #(.width(2)) register_6 (.D(WDSel_D), .Q(WDSel_E), .clk(clk), .clr(CLR));  // open: en
  Register #(.width(1)) register_7 (.D(RegWrite_D), .Q(RegWrite_E), .clk(clk), .clr(CLR));  // open: en
  Register #(.width(4)) register_8 (.D(ALUCtrl_D), .Q(ALUCtrl_E), .clk(clk), .clr(CLR));  // open: en
  Register #(.width(32)) register_9 (.D(RD1_D), .Q(RD1_E), .clk(clk), .clr(CLR));  // open: en
  Register #(.width(32)) register_10 (.D(RD2_D), .Q(RD2_E), .clk(clk), .clr(CLR));  // open: en
  Register #(.width(32)) register_11 (.D(imm32_D), .Q(imm32_E), .clk(clk), .clr(CLR));  // open: en
  Register #(.width(32)) register_12 (.D(PC_8_D), .Q(imm32_E_2), .clk(clk), .clr(CLR));  // open: en
  Register #(.width(2)) register_13 (.D(DMMode_D), .Q(DMMode_E), .clk(clk), .clr(CLR));  // open: en
  Register #(.width(32)) register_14 (.D(PC_D), .Q(PC_E), .clk(clk), .clr(CLR));  // open: en
endmodule

module EX_MEM (
  input  CLR,
  input  MemWrite_E,
  input  [31:0] PC_E,
  input  MemRead_E,
  input  [4:0] RegAddr_E,
  input  [1:0] WDSel_E,
  input  RegWrite_E,
  input  [31:0] Result_E,
  input  [31:0] RD2_E,
  input  [31:0] PC_8_E,
  input  [1:0] DMMode_E,
  output MemWrite_M,
  output [31:0] PC_M,
  output MemRead_M,
  output [4:0] RegAddr_M,
  output [1:0] WDSel_M,
  output RegWrite_M,
  output [31:0] Result_M,
  output [31:0] RD2_M,
  output [31:0] PC_8_M,
  output [1:0] DMMode_M
);

  wire clk;

  Clock clock_1 (.out(clk));
  Register #(.width(1)) register_1 (.D(MemWrite_E), .Q(MemWrite_M), .clk(clk), .clr(CLR));  // open: en
  Register #(.width(1)) register_2 (.D(MemRead_E), .Q(MemRead_M), .clk(clk), .clr(CLR));  // open: en
  Register #(.width(5)) register_3 (.D(RegAddr_E), .Q(RegAddr_M), .clk(clk), .clr(CLR));  // open: en
  Register #(.width(2)) register_4 (.D(WDSel_E), .Q(WDSel_M), .clk(clk), .clr(CLR));  // open: en
  Register #(.width(1)) register_5 (.D(RegWrite_E), .Q(RegWrite_M), .clk(clk), .clr(CLR));  // open: en
  Register #(.width(32)) register_6 (.D(Result_E), .Q(Result_M), .clk(clk), .clr(CLR));  // open: en
  Register #(.width(32)) register_7 (.D(RD2_E), .Q(RD2_M), .clk(clk), .clr(CLR));  // open: en
  Register #(.width(32)) register_8 (.D(PC_8_E), .Q(PC_8_M), .clk(clk), .clr(CLR));  // open: en
  Register #(.width(2)) register_9 (.D(DMMode_E), .Q(DMMode_M), .clk(clk), .clr(CLR));  // open: en
  Register #(.width(32)) register_10 (.D(PC_E), .Q(PC_M), .clk(clk), .clr(CLR));  // open: en
endmodule

module MEM_WB (
  input  CLR,
  input  [31:0] PC_M,
  input  [4:0] RegAddr_M,
  input  [1:0] WDSel_M,
  input  RegWrite_M,
  input  [31:0] Result_M,
  input  [31:0] RD_M,
  input  [31:0] PC_8_M,
  output [31:0] PC_W,
  output [4:0] RegAddr_W,
  output [1:0] WDSel_W,
  output RegWrite_W,
  output [31:0] Result_W,
  output [31:0] RD_W,
  output [31:0] PC_8_W
);

  wire clk;

  Clock clock_1 (.out(clk));
  Register #(.width(32)) register_1 (.D(PC_M), .Q(PC_W), .clk(clk), .clr(CLR));  // open: en
  Register #(.width(5)) register_2 (.D(RegAddr_M), .Q(RegAddr_W), .clk(clk), .clr(CLR));  // open: en
  Register #(.width(2)) register_3 (.D(WDSel_M), .Q(WDSel_W), .clk(clk), .clr(CLR));  // open: en
  Register #(.width(1)) register_4 (.D(RegWrite_M), .Q(RegWrite_W), .clk(clk), .clr(CLR));  // open: en
  Register #(.width(32)) register_5 (.D(Result_M), .Q(Result_W), .clk(clk), .clr(CLR));  // open: en
  Register #(.width(32)) register_6 (.D(RD_M), .Q(RD_W), .clk(clk), .clr(CLR));  // open: en
  Register #(.width(32)) register_7 (.D(PC_8_M), .Q(PC_8_W), .clk(clk), .clr(CLR));  // open: en
endmodule
